# Fritzing sketch Universal Shield (saved by Fritzing 0.9.3b)
circuit board: 8.53488cm x 5.63626cm
breadboards: 1

parts:
  Nano1 = Arduino Nano v2.3
  WeMos_D1_Mini1 = WeMos D1 Mini  # not connected
  IC3 = Darlington Driver [package=dil18]
  IC2 = Darlington Driver [package=dil18]
  Q1 = MOSFET-NCHANNEL [package=to220v]
  Q2 = MOSFET-NCHANNEL [package=to220v]
  Q3 = MOSFET-NCHANNEL [package=to220v]
  Q4 = MOSFET-NCHANNEL [package=to220v]
  IC1 = Voltage Regulator [package=78xxl]  # not connected
  J1 = double row smd female pin header, 40 pins [form="♀ (female)"]  # not connected
  Part1 = Arduino Uno (Rev3)  # not connected
  J2 = female pin header, 10 pins [form="♀ (female)"]
  R1 = Resistor [tolerance=±5% resistance=220 package=THT]
  R2 = Resistor [tolerance=±5% resistance=220 package=THT]
  R3 = Resistor [tolerance=±5% resistance=220 package=THT]
  R4 = Resistor [tolerance=±5% resistance=220 package=THT]
  R5 = Resistor [tolerance=±5% resistance=220 package=THT]
  R6 = Resistor [tolerance=±5% resistance=220 package=THT]
  R7 = Resistor [tolerance=±5% resistance=220 package=THT]
  R8 = Resistor [tolerance=±5% resistance=220 package=THT]
  RHT1 = Humidity and Temperature Sensor RHT03  # not connected
  U1 = PCA9306 [package=psop-8]  # not connected

nets:
  N1: Nano1.GND, IC3.9, IC2.9, J2.pin1
  N2: Nano1.D2, IC2.8
  N3: Nano1.D3, IC2.7, R3.Pin_1
  N4: Nano1.D4, IC2.6
  N5: Nano1.D5, IC2.5, R1.Pin_1
  N6: Nano1.D6, IC2.4, R4.Pin_0
  N7: Nano1.D7, IC2.3
  N8: Nano1.D8, IC2.2
  N9: Nano1.D9, IC2.1, R2.Pin_0
  N10: Nano1.A7, R6.Pin_0
  N11: Nano1.A6, R5.Pin_0
  N12: Nano1.A5, R7.Pin_1
  N13: Nano1.A4, R8.Pin_1
  N14: IC2.10, J2.pin10
  N15: IC2.11, J2.pin9
  N16: IC2.12, J2.pin8
  N17: IC2.13, J2.pin7
  N18: IC2.14, J2.pin6
  N19: IC2.15, J2.pin5
  N20: IC2.16, J2.pin4
  N21: IC2.17, J2.pin3
  N22: IC2.18, J2.pin2
  N23: Q1.G, R1.Pin_0, R7.Pin_0
  N24: Q1.S, Q2.S, Q3.S, Q4.S
  N25: Q2.G, R3.Pin_0, R8.Pin_0
  N26: Q3.G, R2.Pin_1, R5.Pin_1
  N27: Q4.G, R4.Pin_1, R6.Pin_1
